# Fritzing sketch shield (saved by Fritzing 0.9.2b)
breadboards: 1

parts:
  Bauteil1 = Arduino Uno (Rev3)
  Bauteil2 = 4pin connector sideways
  Bauteil3 = 4pin connector sideways
  R2 = Resistor [tolerance=±5% resistance=10k package=THT]
  R3 = Resistor [tolerance=±5% resistance=10k package=THT]
  Bauteil4 = LG_FPC_10_1mm
  Bauteil5 = relay d2a050000
  Bauteil6 = relay d2a050000
  J1 = Piezo Speaker

nets:
  N1: Bauteil1.D11_PWM/MOSI, Bauteil3.pin2, R3.Pin_1
  N2: Bauteil1.D12/MISO, Bauteil3.pin1, R2.Pin_1
  N3: Bauteil1.GND, Bauteil2.pin0, Bauteil3.pin0, R2.Pin_0, R3.Pin_0, Bauteil5.pin6, Bauteil6.pin6, J1.pin1
  N4: Bauteil1.D2, Bauteil2.pin2
  N5: Bauteil1.D3_PWM, Bauteil2.pin1
  N6: Bauteil1.D5_PWM, J1.pin2
  N7: Bauteil1.D6_PWM, Bauteil5.pin2
  N8: Bauteil1.D7, Bauteil6.pin2
  N9: Bauteil1.5V, Bauteil2.pin3
  N10: Bauteil4.pin_4, Bauteil5.pin1, Bauteil6.pin1
  N11: Bauteil4.pin_5, Bauteil5.pin7
  N12: Bauteil4.pin_6, Bauteil6.pin7

custom parts:
  LG_FPC_10_1mm: würth ffc/fpc 10 connector x 1mm raster
